# Fritzing sketch Lab2-Activity2 (saved by Fritzing 1.0.3b)
breadboards: 1

parts:
  M1 = nRF52 DK
  R1 = Resistor [tolerance=±5% power=0.25W resistance=330 package=THT]
  LED1 = LED - 5mm [color="Red (633nm)" current=0.030A package="5 mm [THT]"]
  R2 = Resistor [tolerance=±5% power=0.25W resistance=330 package=THT]
  LED2 = LED - 5mm [color="Green (560nm)" current=0.030A package="5 mm [THT]"]

nets:
  N1: M1.Pin_53, M1.Pin_55, LED1.cathode, LED2.cathode
  N2: M1.Pin_59, R2.Pin_1
  N3: M1.Pin_65, R1.Pin_1
  N4: R1.Pin_0, LED1.anode
  N5: R2.Pin_0, LED2.anode

custom parts:
  nRF52 DK: The nRF52 DK is a versatile single board development kit for Bluetooth® Smart, ANT and 2.4GHz proprietary applications using the nRF52832 SoC. This kit supports development for the nRF52832 SoC. The kit is hardware compatible with the Arduino Uno Revision 3 standard, making it possible to use 3rd-party shields that are compatible to this standard. An NFC antenna can be connected the kit to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
