# Fritzing sketch Lab3-Activity2 (saved by Fritzing 1.0.3b)
breadboards: 1

parts:
  M1 = nRF52 DK
  U1 = SWITCH_SPDT [package=kps-1290]
  R1 = Resistor [tolerance=±5% power=0.25W resistance=330 package=THT]
  R2 = Resistor [tolerance=±5% power=0.25W resistance=330 package=THT]
  LED1 = LED - 5mm [color="Red (633nm)" current=0.030A package="5 mm [THT]"]
  LED2 = LED - 5mm [color="Green (555nm)" current=0.030A package="5 mm [THT]"]

nets:
  N1: M1.Pin_42, M1.Pin_43, M1.Pin_44, U1.O
  N2: M1.Pin_55, U1.S, R1.Pin_0, R2.Pin_0
  N3: M1.Pin_59, U1.P
  N4: M1.Pin_62, M1.Pin_63, LED2.anode
  N5: M1.Pin_65, LED1.anode
  N6: R1.Pin_1, LED2.cathode
  N7: R2.Pin_1, LED1.cathode

custom parts:
  nRF52 DK: The nRF52 DK is a versatile single board development kit for Bluetooth® Smart, ANT and 2.4GHz proprietary applications using the nRF52832 SoC. This kit supports development for the nRF52832 SoC. The kit is hardware compatible with the Arduino Uno Revision 3 standard, making it possible to use 3rd-party shields that are compatible to this standard. An NFC antenna can be connected the kit to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
