# Fritzing sketch Photointerrupter Circuit (saved by Fritzing 1.0.3b)
breadboards: 1

parts:
  Optointerrupter_(H21A1) = CNZ1120 [package=cnz1120]
  R1 = Resistor [tolerance=±5% resistance=330 power=0.25W package=THT]
  R2 = Resistor [tolerance=±5% resistance=10k power=0.25W package=THT]
  M1 = nRF52 DK

nets:
  N1: Optointerrupter_(H21A1).1, R1.Pin_1
  N2: Optointerrupter_(H21A1).2, Optointerrupter_(H21A1).4, M1.Pin_53, M1.Pin_55
  N3: Optointerrupter_(H21A1).3, R2.Pin_1, M1.Pin_59
  N4: R1.Pin_0, R2.Pin_0, M1.Pin_43

custom parts:
  nRF52 DK: The nRF52 DK is a versatile single board development kit for Bluetooth® Smart, ANT and 2.4GHz proprietary applications using the nRF52832 SoC. This kit supports development for the nRF52832 SoC. The kit is hardware compatible with the Arduino Uno Revision 3 standard, making it possible to use 3rd-party shields that are compatible to this standard. An NFC antenna can be connected the kit to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
